# Fritzing sketch RobotScetch v1 (saved by Fritzing 0.9.3b)
circuit board: 8.46667cm x 5.64444cm
breadboards: 1

parts:
  IC1 = H-Bridge [package=THT]
  R1 = Resistor [tolerance=±5% resistance=10k package=THT]
  R2 = Resistor [tolerance=±5% resistance=10k package=THT]
  R3 = Resistor [tolerance=±5% resistance=10k package=THT]
  R4 = Resistor [tolerance=±5% resistance=10k package=THT]
  R5 = Photocell (LDR) [package=THT]
  R6 = Photocell (LDR) [package=THT]
  R7 = Photocell (LDR) [package=THT]
  R8 = Photocell (LDR) [package=THT]
  M1 = DC Motor
  M2 = DC Motor
  J1 = Infrared Proximity Sensor
  Power_plug1 = Power plug
  Bauteil1 = Arduino Uno (Rev3)

nets:
  N1: IC1.1_2EN, Bauteil1.D11_PWM/MOSI
  N2: IC1.1A, Bauteil1.D13/SCK
  N3: IC1.1Y, M2.pin_1
  GND: IC1.GND1, IC1.GND4, R1.Pin_0, R2.Pin_0, R3.Pin_0, R4.Pin_0, J1.GND, Power_plug1.GND, Bauteil1.GND
  N4: IC1.2Y, M2.pin_2
  N5: IC1.2A, Bauteil1.D12/MISO
  N6: IC1.VCC2, Power_plug1.VCC
  N7: IC1.3_4EN, Bauteil1.D6_PWM
  N8: IC1.3A, Bauteil1.D4
  N9: IC1.3Y, M1.pin_2
  N10: IC1.4Y, M1.pin_1
  N11: IC1.4A, Bauteil1.D2
  VCC: IC1.VCC1, R5.pin_0, R6.pin_0, R7.pin_0, R8.pin_0, J1.Vcc, Bauteil1.5V
  N12: R1.Pin_1, R8.pin_1, Bauteil1.A3
  N13: R2.Pin_1, R6.pin_1, Bauteil1.A0
  N14: R3.Pin_1, R7.pin_1, Bauteil1.A1
  N15: R4.Pin_1, R5.pin_1, Bauteil1.A2
  N16: J1.Vout, Bauteil1.A4/SDA

notes:
  to batterie for motor power (9V)
  To batterie for Arduino
  9V
  5V Line
